# Fritzing sketch Circuit Diagram (saved by Fritzing 0.9.3b)

parts:
  Digispark1 = Digispark
  Part1 = NeoPixel Stick [part_number=1426]

nets:
  VCC: Digispark1.VCC, Part1.+5V
  GND: Digispark1.GND, Part1.GND
  N1: Digispark1.P4, Part1.DATAIN

custom parts:
  Digispark: The Digispark is an Attiny85 based microcontroller development board similar to the Arduino line, only cheaper, smaller, and a bit less powerful. With a whole host of shields to extend its functionality and the ability to use the familiar Arduino IDE the Digispark is a great way to jump into electronics, or perfect for when an Arduino is too big or too much.
  NeoPixel Stick: Make your own little LED strip arrangement with this stick of NeoPixel LEDs. We crammed 8 of the tiny 5050 (5mm x 5mm) smart RGB LEDs onto a PCB with mounting holes and a chainable design. Use only one microcontroller pin to control as many as you can chain together! Each LED is addressable as the driver chip is inside the LED. Each one has ~18mA constant current drive so the color will be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
